# Fritzing sketch Schema Elettrico (saved by Fritzing 0.9.3b)
breadboards: 3

parts:
  Modulo_Bluetooth_HC-05 = Bluetooth HC-05 Macho  # not connected
  part = Resistor [tolerance=±5% resistance=1k package=THT]
  part_2 = Resistor [tolerance=±5% resistance=2k package=THT]
  Arduino_UNO = Arduino Uno (Rev3) - ICSP
  part_3 = DRV 8825 Stepper Motor Carrier, High Current [part_number="DRV 8825"]
  WeMos_D1_Mini_Relay_Shield_V1 = WeMos D1 Mini Relay Shield V2
  WeMos_D1_Mini_Relay_Shield_V2 = WeMos D1 Mini Relay Shield V2
  WeMos_D1_Mini_Relay_Shield_V3 = WeMos D1 Mini Relay Shield V2
  WeMos_D1_Mini_Relay_Shield_V4 = WeMos D1 Mini Relay Shield V2
  WeMos_D1_Mini_Relay_Shield_V5 = WeMos D1 Mini Relay Shield V2
  LED1 = LED - 5mm [color="Red (633nm)" package="5 mm [THT]"]
  LED2 = LED - 5mm [color="Red (633nm)" package="5 mm [THT]"]
  LED3 = LED - 5mm [color="Red (633nm)" package="5 mm [THT]"]
  LED4 = LED - 5mm [color="Red (633nm)" package="5 mm [THT]"]
  LED5 = LED - 5mm [color="Yellow (595nm)" package="5 mm [THT]"]
  LED6 = LED - 5mm [color="Yellow (595nm)" package="5 mm [THT]"]
  LED7 = LED - 5mm [color="Yellow (595nm)" package="5 mm [THT]"]
  LED8 = LED - 5mm [color="Yellow (595nm)" package="5 mm [THT]"]
  LED9 = LED - 5mm [color="Yellow (595nm)" package="5 mm [THT]"]
  LED10 = LED - 5mm [color="Yellow (595nm)" package="5 mm [THT]"]
  LED11 = LED - 5mm [color="Yellow (595nm)" package="5 mm [THT]"]
  LED12 = LED - 5mm [color="Yellow (595nm)" package="5 mm [THT]"]
  LED13 = LED - 5mm [color="Green (570nm)" package="5 mm [THT]"]
  LED14 = LED - 5mm [color="Green (570nm)" package="5 mm [THT]"]
  LED15 = LED - 5mm [color="Green (570nm)" package="5 mm [THT]"]
  LED16 = LED - 5mm [color="Green (570nm)" package="5 mm [THT]"]
  LED17 = LED - 5mm [color="Green (570nm)" package="5 mm [THT]"]
  LED18 = LED - 5mm [color="Green (570nm)" package="5 mm [THT]"]
  LED19 = LED - 5mm [color="Green (570nm)" package="5 mm [THT]"]
  LED20 = LED - 5mm [color="Green (570nm)" package="5 mm [THT]"]
  LED21 = LED - 5mm [color="Blue (430nm)" package="5 mm [THT]"]
  LED22 = LED - 5mm [color="Blue (430nm)" package="5 mm [THT]"]
  LED23 = LED - 5mm [color="Blue (430nm)" package="5 mm [THT]"]
  LED24 = LED - 5mm [color="Blue (430nm)" package="5 mm [THT]"]
  LED25 = LED - 5mm [color="Blue (430nm)" package="5 mm [THT]"]
  LED26 = LED - 5mm [color="Blue (430nm)" package="5 mm [THT]"]
  LED27 = LED - 5mm [color="Blue (430nm)" package="5 mm [THT]"]
  LED28 = LED - 5mm [color="Blue (430nm)" package="5 mm [THT]"]
  LED29 = LED - 5mm [color="White (4500K)" package="5 mm [THT]"]
  LED30 = LED - 5mm [color="White (4500K)" package="5 mm [THT]"]
  LED32 = LED - 5mm [color="White (4500K)" package="5 mm [THT]"]
  LED33 = LED - 5mm [color="White (4500K)" package="5 mm [THT]"]
  LED34 = LED - 5mm [color="White (4500K)" package="5 mm [THT]"]
  LED35 = LED - 5mm [color="White (4500K)" package="5 mm [THT]"]
  LED36 = LED - 5mm [color="White (4500K)" package="5 mm [THT]"]
  LED31 = smd LED [color="White (4500K)" package="1206 [SMD]"]
  R3 = Resistor [tolerance=±5% resistance=666 package=THT]
  R5 = Resistor [tolerance=±5% resistance=666 package=THT]
  R6 = Resistor [tolerance=±5% resistance=666 package=THT]
  R7 = Resistor [tolerance=±5% resistance=666 package=THT]
  R8 = Resistor [tolerance=±5% resistance=666 package=THT]
  part_4 = Resistor [tolerance=±5% resistance=666 package=THT]
  R10 = Resistor [tolerance=±5% resistance=666 package=THT]
  R11 = Resistor [tolerance=±5% resistance=666 package=THT]
  R12 = Resistor [tolerance=±5% resistance=400 package=THT]
  R13 = Resistor [tolerance=±5% resistance=400 package=THT]
  part_5 = Resistor [tolerance=±5% resistance=400 package=THT]
  R15 = Resistor [tolerance=±5% resistance=400 package=THT]
  R16 = Resistor [tolerance=±5% resistance=400 package=THT]
  R17 = Resistor [tolerance=±5% resistance=400 package=THT]
  R18 = Resistor [tolerance=±5% resistance=400 package=THT]
  R19 = Resistor [tolerance=±5% resistance=400 package=THT]
  R20 = Resistor [tolerance=±5% resistance=673 package=THT]
  R22 = Resistor [tolerance=±5% resistance=673 package=THT]
  R23 = Resistor [tolerance=±5% resistance=673 package=THT]
  R24 = Resistor [tolerance=±5% resistance=673 package=THT]
  R25 = Resistor [tolerance=±5% resistance=673 package=THT]
  part_6 = Resistor [tolerance=±5% resistance=673 package=THT]
  R27 = Resistor [tolerance=±5% resistance=673 package=THT]
  R28 = Resistor [tolerance=±5% resistance=673 package=THT]
  part_7 = Resistor [tolerance=±5% resistance=463 package=THT]
  R30 = Resistor [tolerance=±5% resistance=463 package=THT]
  R31 = Resistor [tolerance=±5% resistance=463 package=THT]
  R32 = Resistor [tolerance=±5% resistance=463 package=THT]
  R33 = Resistor [tolerance=±5% resistance=566 package=THT]
  R34 = Resistor [tolerance=±5% resistance=566 package=THT]
  part_8 = Resistor [tolerance=±5% resistance=566 package=THT]
  R36 = Resistor [tolerance=±5% resistance=566 package=THT]
  R37 = Resistor [tolerance=±5% resistance=566 package=THT]
  R38 = Resistor [tolerance=±5% resistance=566 package=THT]
  R39 = Resistor [tolerance=±5% resistance=566 package=THT]
  R40 = Resistor [tolerance=±5% resistance=566 package=THT]
  EXTERNAL_POWER_SUPPLY_12V = Power Jack [package=power_jack_slot]
  part_9 = Electrolytic Capacitor [capacitance=100µF package="200 mil [THT, electrolytic]"]  # not connected
  Nema_17 = Stepper Motor - Bipolar

nets:
  N1: part.Pin_0, Arduino_UNO.D1/TX
  N2: part.Pin_1, part_2.Pin_0
  N3: part_2.Pin_1, Arduino_UNO.GND
  N4: Arduino_UNO.D3_PWM, part_3.STEP
  N5: Arduino_UNO.D4, part_3.DIRECTION
  N6: Arduino_UNO.5V, part_3.RESET, part_3.SLEEP, part_3.GROUND_LOG
  N7: part_3.VOLTAGE_ST/_MT, EXTERNAL_POWER_SUPPLY_12V.PWR
  N8: part_3.GROUND_ST/_MT, LED1.cathode, LED2.cathode, LED3.cathode, LED4.cathode, LED5.cathode, LED6.cathode, LED7.cathode, LED8.cathode, LED9.cathode, LED10.cathode, LED11.cathode, LED12.cathode, LED13.cathode, EXTERNAL_POWER_SUPPLY_12V.GNDBREAK
  N9: part_3.OUT_2B, Nema_17.A
  N10: part_3.OUT_2A, Nema_17.C
  N11: part_3.OUT_1A, Nema_17.B
  N12: part_3.OUT_1B, Nema_17.D
  N13: WeMos_D1_Mini_Relay_Shield_V1.COM, WeMos_D1_Mini_Relay_Shield_V2.COM, WeMos_D1_Mini_Relay_Shield_V3.COM, WeMos_D1_Mini_Relay_Shield_V4.COM, WeMos_D1_Mini_Relay_Shield_V5.COM
  N14: WeMos_D1_Mini_Relay_Shield_V1.NO, R12.Pin_0, R13.Pin_0, part_5.Pin_0, R15.Pin_0, R16.Pin_0, R17.Pin_0, R18.Pin_0, R19.Pin_0
  N15: WeMos_D1_Mini_Relay_Shield_V2.NO, R33.Pin_0, R34.Pin_0, part_8.Pin_0, R36.Pin_0, R37.Pin_0, R38.Pin_0, R39.Pin_0, R40.Pin_0
  N16: WeMos_D1_Mini_Relay_Shield_V5.NO, R20.Pin_0, R22.Pin_0, R23.Pin_0, R24.Pin_0, R25.Pin_0, part_6.Pin_0, R27.Pin_0, R28.Pin_0
  N17: LED1.anode, part_7.Pin_1
  N18: LED2.anode, R30.Pin_1
  N19: LED3.anode, R31.Pin_1
  N20: LED4.anode, R32.Pin_1
  N21: LED5.anode, R28.Pin_1
  N22: LED6.anode, R27.Pin_1
  N23: LED7.anode, R25.Pin_1
  N24: LED8.anode, part_6.Pin_1
  N25: LED9.anode, R24.Pin_1
  N26: LED10.anode, R23.Pin_1
  N27: LED11.anode, R22.Pin_1
  N28: LED12.anode, R20.Pin_1
  N29: LED13.anode, R11.Pin_1
  N30: LED14.cathode, LED15.cathode, LED16.cathode, LED17.cathode, LED18.cathode, LED19.cathode, LED20.cathode, LED21.cathode, LED22.cathode, LED23.cathode, LED24.cathode, LED25.cathode, LED26.cathode, LED27.cathode, LED28.cathode, LED29.cathode, LED30.cathode, LED32.cathode, LED33.cathode, LED34.cathode, LED35.cathode, LED36.cathode
  N31: LED14.anode, R10.Pin_1
  N32: LED15.anode, part_4.Pin_1
  N33: LED16.anode, R8.Pin_1
  N34: LED17.anode, R7.Pin_1
  N35: LED18.anode, R5.Pin_1
  N36: LED19.anode, R6.Pin_1
  N37: LED20.anode, R3.Pin_1
  N38: LED21.anode, R39.Pin_1
  N39: LED22.anode, R33.Pin_1
  N40: LED23.anode, R34.Pin_1
  N41: LED24.anode, part_8.Pin_1
  N42: LED25.anode, R36.Pin_1
  N43: LED26.anode, R37.Pin_1
  N44: LED27.anode, R38.Pin_1
  N45: LED28.anode, R40.Pin_1
  N46: LED29.anode, R15.Pin_1
  N47: LED30.anode, R16.Pin_1
  N48: LED32.anode, R12.Pin_1
  N49: LED33.anode, part_5.Pin_1
  N50: LED34.anode, R17.Pin_1
  N51: LED35.anode, R18.Pin_1
  N52: LED36.anode, R13.Pin_1
  N53: LED31.anode, R19.Pin_1
  N54: R3.Pin_0, R5.Pin_0, R6.Pin_0, R7.Pin_0, R8.Pin_0, part_4.Pin_0, R10.Pin_0, R11.Pin_0
  N55: part_7.Pin_0, R30.Pin_0, R31.Pin_0, R32.Pin_0

notes:
  L'alimentazione è fornita da una batteria a 12 V minimo;
  su Frtitzing non era presentea.
  Partitori di corrente per ogni colore, comandabili separatamente grazie all'utilizzo di 5 relè
  Ogni Relay ha in ingresso i due capi positivi della batteria, positivo e negativo di arduino e segnale digitale di arduino
  Pin collegati ad arduino
  0 TX HC-05
  1 RX HC-05
  2 Dir Nema 17
  3 Step Nema 17
  5 Rosso
  6 Blue
  8 verde
  9 Bianco
  10 giallo
  Nel progetto il circuito per gestire il nema 17 è integrrato all'interno di una schedina.
  I pin che escono e vanno all'uscita sono 3, Dir e Step vanno ad arduino l'altro può comodamente andare a gnd
